// Logisim project alu.circ as structural Verilog: 1 circuit, main circuit alu
module alu (
  input  [31:0] A,
  input  [31:0] B,
  input  [3:0] ALUSel,
  output [31:0] Result
);

  wire [31:0] add0, divider_2_rem, shifter_1_out, undriven;

  Adder #(.width(32)) adder_1 (.a(A), .b(B), .out(add0));  // open: cin, cout
  // AND_Gate and_1 has open pins: in0=A, in1=B, out=open
  // OR_Gate or_1 has open pins: in0=A, in1=B, out=open
  // XOR_Gate xor_1 has open pins: in0=A, in1=B, out=open
  Shifter #(.width(32)) shifter_1 (.in(A), .out(shifter_1_out));  // open: dist
  Shifter #(.width(32)) shifter_2 (.in(A));  // open: dist, out
  Shifter #(.width(32)) shifter_3 (.in(A));  // open: dist, out
  Comparator #(.width(32)) comparator_1 (.a(A), .b(B));  // open: gt, eq, lt
  Divider #(.width(32)) divider_1 (.a(B), .b(A), .upper(undriven));  // open: out, rem
  Divider #(.width(32)) divider_2 (.a(B), .b(A), .rem(divider_2_rem));  // open: out, upper
  Multiplier #(.width(32)) multiplier_1 (.a(B), .b(A));  // open: out, cin, cout
  Multiplier #(.width(32)) multiplier_2 (.a(A), .b(B));  // open: out, cin, cout
  Subtractor #(.width(32)) subtractor_1 (.a(A), .b(B));  // open: out, bin, bout
  Multiplexer #(.width(32), .enable("false")) multiplexer_1 (.in0(B));  // open: in1, out, sel

  // Notes on the sheet:
  //   INPUTS to your circuit
  //   and
  //   or
  //   xor
  //   srl
  //   sra
  //   sll
  //   slt
  //   divu
  //   remu
  //   mul
  //   mulhu
  //   sub
  //   bsel
  //   DON'T CHANGE THE LOCATIONS OF THE INPUTS AND OUTPUTS!
  //   OUTPUT from your circuit
endmodule
