// Logisim project cpu.circ as structural Verilog: 4 circuits, main circuit main
module main (
  input  [31:0] INSTRUCTION,
  input  CLOCK,
  output [31:0] PROGRAM_COUNTER,
  output [31:0] ra,
  output [31:0] sp,
  output [31:0] t0,
  output [31:0] t1,
  output [31:0] t2,
  output [31:0] s0,
  output [31:0] s1,
  output [31:0] a0
);

  wire BrEq, BrLt, BrUn, DMEM_p1, DMEM_p4, RegWEn, undriven;
  wire [2:0] immSel;
  wire [3:0] ALUSel;
  wire [6:0] INSTRUCTION_OUT;
  wire [24:0] imm;
  wire [31:0] adder_1_out, ALU_Out, imm_Extended, multiplexer_1_out, rs1_Out, rs2_Out;

  Adder #(.width(32)) adder_1 (.a(PROGRAM_COUNTER), .b(32'h4), .out(adder_1_out));  // open: cin, cout
  Register #(.width(32)) register_1 (.D(INSTRUCTION), .clk(CLOCK), .Q({imm, INSTRUCTION_OUT}));  // open: en, clr
  Register #(.width(32)) PC (.D(adder_1_out), .clk(CLOCK), .Q(PROGRAM_COUNTER));  // open: en, clr
  immGen immgen_1 (.imm_Out(imm_Extended), .ins_In(imm), .immSel(immSel));
  control control_1 ();  // open: inst_In, BrLt, BrEq, PCSel, RegWEn, ImmSel, BSel, ASel, ALUSel, MemRW, WBSel, out_12
  regfile_main RegFile (
    .rs2(imm[17:13]), .rd(imm[4:0]), .Read_Data_1(rs1_Out), .Read_Data_2(rs2_Out), .ra(ra), .sp(sp), .t0(t0),
    .t1(t1), .t2(t2), .s0(s0), .s1(s1), .a0(a0), .rs1(imm[12:8]), .Write_Data(ALU_Out), .RegWEn(RegWEn),
    .clk(CLOCK));
  branchComp branchcomp_1 (.rs1(rs1_Out), .rs2(rs2_Out), .BrUn(BrUn), .BrEq(BrEq), .BrLt(BrLt));
  Multiplexer #(.width(32), .enable("false")) multiplexer_1 (
    .in0(rs2_Out), .in1(imm_Extended), .out(multiplexer_1_out), .sel(undriven));
  alu Arithmetic_Logic_Unit (.Result(ALU_Out), .ALUSel(ALUSel), .A(rs1_Out), .B(multiplexer_1_out));
  // mem_main DMEM: pin names not known; wires that end beside it: DMEM_p1, DMEM_p1, CLOCK, DMEM_p4

  // Other names for the same wires on the sheet: clk = CLOCK; INSTRUCTION_OUT[31:7] = imm; rd[4:0] = imm[4:0];
  //   rs1_In[4:0] = imm[12:8]; rs2_In[4:0] = imm[17:13]

  // Notes on the sheet:
  //   Output
  //   IMEM (do **NOT** move this)
  //   Inputs
  //   Inputs/Outputs for testing. Do **NOT** move these.
endmodule

module immGen (
  input  [24:0] ins_In,
  input  [2:0] immSel,
  output [31:0] imm_Out
);

  wire [31:0] I, S, SB, U, UJ;

  assign I = {{20{ins_In[24]}}, ins_In[24:13]};  // Bit_Extender bit_extender_1
  assign U = {{12{ins_In[24]}}, ins_In[24:5]};  // Bit_Extender bit_extender_2
  assign S = {{20{ins_In[24]}}, {ins_In[24:18], ins_In[4:0]}};  // Bit_Extender bit_extender_3
  assign SB = {{19{ins_In[24]}}, {ins_In[24], ins_In[0], ins_In[23:18], ins_In[4:1], 1'b0}};  // Bit_Extender bit_extender_4
  assign UJ = {{11{ins_In[24]}}, {ins_In[24], ins_In[12:5], ins_In[13], ins_In[23:14], 1'b0}};  // Bit_Extender bit_extender_5
  Multiplexer #(.select(3), .width(32), .enable("false")) multiplexer_1 (
    .in0(I), .in1(S), .in2(SB), .in3(U), .in4(UJ), .out(imm_Out), .sel(immSel));  // open: in5, in6, in7

  // Other names for the same wires on the sheet: Instruction_In[24:0] = ins_In
endmodule

module control (
  input  [31:0] inst_In,
  input  BrLt,
  input  BrEq,
  output PCSel,
  output RegWEn,
  output [3:0] ImmSel,
  output BSel,
  output ASel,
  output [4:0] ALUSel,
  output MemRW,
  output WBSel,
  output [7:0] out_12
);

  ROM #(.addrWidth(24), .dataWidth(6)) rom_1 ();  // open: addr, data

  // Notes on the sheet:
  //   contents of rom_1 (hex, n*v repeats v):
  //   0 0 0 1 11*0 1
endmodule

module branchComp (
  input  [31:0] rs1,
  input  [31:0] rs2,
  input  BrUn,
  output BrEq,
  output BrLt
);

  wire BrEqSigned, BrEqUnsigned, BrLtSigned, BrLtUnsigned;

  Comparator #(.width(32)) comparator_1 (.a(rs1), .b(rs2), .eq(BrEqSigned), .lt(BrLtSigned));  // open: gt
  Comparator #(.width(32), .mode("unsigned")) comparator_2 (
    .a(rs1), .b(rs2), .eq(BrEqUnsigned), .lt(BrLtUnsigned));  // open: gt
  Multiplexer #(.enable("false")) multiplexer_1 (.in0(BrLtSigned), .in1(BrLtUnsigned), .out(BrLt), .sel(BrUn));
  Multiplexer #(.enable("false")) multiplexer_2 (.in0(BrEqSigned), .in1(BrEqUnsigned), .out(BrEq), .sel(BrUn));
endmodule
